// Logisim project for bonus.circ as structural Verilog: 15 circuits, main circuit main
module main (
);

  wire alu_1_ble_zero, alu_control2_1_call, alu_control2_1_jump, alu_control2_1_reboot, alu_control2_1_rtn,
       and_1_out, Branch_Jump, clock, clock_1_out, control_unit_1_halt, control_unit_1_regdst,
       ex_mem_1_halt_2, exwrite, halt, hazard_flushid, hazard_flushif, hazard_stallid, hazard_stallif,
       id_ex_1_halt_2, memwrite, regread_1_r1, regread_1_r2, rread, w;
  wire [0:0] ex_mem_1_wb_2, id_ex_1_wb_2, mem_wb_1_wb_2;
  wire [1:0] control_unit_1_memtoreg, ex_mem_1_m_2;
  wire [2:0] control_unit_1_branch, ex, id_ex_1_m_2, mem, multiplexer_1_out, wreg;
  wire [3:0] alu_control_1_alu_control_output;
  wire [4:0] control_unit_1_aluop1, id_ex_1_ex_2, if_id_1_instru_2_2;
  wire [10:0] if_id_1_instru_2;
  wire [15:0] adder_1_out, adder_2_out, adder_3_out, alu_1_alu_result, bit_extender_1_out,
       bit_extender_2_out, ex_mem_1_alu_result_2, ex_mem_1_d_2, id_ex_1_imm_2, id_ex_1_pc_1_2, id_ex_1_r1_2,
       id_ex_1_r2_2, if_id_1_pc_1_2, mem_wb_1_alu_result_2, mem_wb_1_d_2, multiplexer_3_out,
       multiplexer_4_out, multiplexer_5_out, multiplexer_6_out, multiplexer_7_out, multiplexer_8_out,
       ram_1_data, register_1_q, register_2_q, registerfile_1_data1, registerfile_1_data2, rom_1_data,
       subtractor_1_out;

  Register #(.width(16)) register_1 (
    .D(multiplexer_7_out), .en(hazard_stallif), .Q(register_1_q), .clk(clock));  // open: clr
  Adder #(.width(16)) adder_1 (.a(register_1_q), .b(16'h1), .out(adder_1_out));  // open: cin, cout
  ROM #(.addrWidth(16), .dataWidth(16)) rom_1 (.addr(register_1_q), .data(rom_1_data));  // open: sel
  IF_ID if_id_1 (
    .PC_1(adder_1_out), .Instru(rom_1_data), .Enable(hazard_stallid), .PC_1_2(if_id_1_pc_1_2),
    .Instru_2({if_id_1_instru_2_2, if_id_1_instru_2}), .clock(clock), .reset(hazard_flushif));
  hazard hazard (
    .r1read(regread_1_r1), .ex(ex), .exwrite(exwrite), .r2(if_id_1_instru_2[7:5]),
    .r1(if_id_1_instru_2[10:8]), .mem(mem), .memwrite(memwrite), .branch___jump(Branch_Jump), .wreg(wreg),
    .W(w), .flushID(hazard_flushid), .r2read(regread_1_r2), .stallIF(hazard_stallif),
    .stallID(hazard_stallid), .flushIF(hazard_flushif));  // open: in_1
  regread regread_1 (
    .op1(if_id_1_instru_2_2[4]), .op2(if_id_1_instru_2_2[3]), .op3(if_id_1_instru_2_2[2]),
    .op4(if_id_1_instru_2_2[1]), .op5(if_id_1_instru_2_2[0]), .r1(regread_1_r1), .r2(regread_1_r2));
  Control_Unit control_unit_1 (
    .op15(if_id_1_instru_2_2[4]), .op14(if_id_1_instru_2_2[3]), .op13(if_id_1_instru_2_2[2]),
    .op12(if_id_1_instru_2_2[1]), .op11(if_id_1_instru_2_2[0]), .RegDst(control_unit_1_regdst),
    .RegWrite(control_unit_1_memtoreg[1]), .ALUSrc(control_unit_1_aluop1[4]),
    .Branch(control_unit_1_branch[0]), .MemRead(control_unit_1_branch[1]),
    .MemWrite(control_unit_1_branch[2]), .MemToReg(control_unit_1_memtoreg[0]),
    .ALUop1(control_unit_1_aluop1[0]), .ALUop2(control_unit_1_aluop1[1]), .ALUop3(control_unit_1_aluop1[2]),
    .ALUop4(control_unit_1_aluop1[3]), .halt(control_unit_1_halt));
  assign bit_extender_1_out = {{11{if_id_1_instru_2[4]}}, if_id_1_instru_2[4:0]};  // Bit_Extender bit_extender_1
  assign bit_extender_2_out = {{5{if_id_1_instru_2[10]}}, if_id_1_instru_2};  // Bit_Extender bit_extender_2
  Multiplexer #(.width(3)) multiplexer_1 (
    .in0(if_id_1_instru_2[7:5]), .in1(if_id_1_instru_2[4:2]), .out(multiplexer_1_out),
    .sel(control_unit_1_regdst));  // open: en
  registerfile registerfile_1 (
    .write(w), .read_register_1(if_id_1_instru_2[10:8]), .write_Register(wreg),
    .read_register_2(if_id_1_instru_2[7:5]), .clock(clock), .write_data(multiplexer_8_out),
    .data1(registerfile_1_data1), .data2(registerfile_1_data2));
  Clock clock_1 (.out(clock_1_out));
  Multiplexer #(.enable("false")) multiplexer_2 (.in0(clock_1_out), .in1(1'b0), .out(clock), .sel(halt));
  ID___EX id_ex_1 (
    .WB(control_unit_1_memtoreg), .M(control_unit_1_branch), .EX(control_unit_1_aluop1),
    .PC_1(if_id_1_pc_1_2), .r1(registerfile_1_data1), .r2(registerfile_1_data2), .w(multiplexer_1_out),
    .imm(bit_extender_1_out), .WB_2({exwrite, id_ex_1_wb_2[0]}), .M_2(id_ex_1_m_2), .EX_2(id_ex_1_ex_2),
    .PC_1_2(id_ex_1_pc_1_2), .r1_2(id_ex_1_r1_2), .r2_2(id_ex_1_r2_2), .w_2(ex), .imm_2(id_ex_1_imm_2),
    .clock(clock), .reset(hazard_flushid), .halt(control_unit_1_halt), .halt_2(id_ex_1_halt_2));
  Register #(.width(16)) register_2 (.D(adder_1_out), .en(rread), .Q(register_2_q), .clk(clock));  // open: clr
  Subtractor #(.width(16)) subtractor_1 (.a(id_ex_1_pc_1_2), .b(16'h1), .out(subtractor_1_out));  // open: bin, bout
  Multiplexer #(.width(16)) multiplexer_3 (
    .in0(id_ex_1_r2_2), .in1(id_ex_1_imm_2), .out(multiplexer_3_out), .sel(id_ex_1_ex_2[4]));  // open: en
  ALU_Control alu_control_1 (
    .ALUop1(id_ex_1_ex_2[0]), .ALUop2(id_ex_1_ex_2[1]), .ALUop3(id_ex_1_ex_2[2]), .ALUop4(id_ex_1_ex_2[3]),
    .ALU_control_output(alu_control_1_alu_control_output));  // open: out_5
  ALU_Control2 alu_control2_1 (
    .ALUop1(id_ex_1_ex_2[0]), .ALUop2(id_ex_1_ex_2[1]), .ALUop3(id_ex_1_ex_2[2]), .ALUop4(id_ex_1_ex_2[3]),
    .jump(alu_control2_1_jump), .call(alu_control2_1_call), .rtn(alu_control2_1_rtn),
    .reboot(alu_control2_1_reboot));
  Adder #(.width(16)) adder_2 (.a(subtractor_1_out), .b(id_ex_1_imm_2), .out(adder_2_out));  // open: cin, cout
  ALU alu_1 (
    .Data1(id_ex_1_r1_2), .Data2(multiplexer_3_out), .ALU_sel(alu_control_1_alu_control_output),
    .ALU_result(alu_1_alu_result), .BLE_ZERO(alu_1_ble_zero));  // open: _0000data1self, _0001plus, _0010and, _0011or, _0100negdata1, SLT0110, shiftleft0111, shiftright1000, _1001, out_15
  Multiplexer #(.width(16)) multiplexer_4 (
    .in0(id_ex_1_pc_1_2), .in1(adder_2_out), .out(multiplexer_4_out), .sel(and_1_out));  // open: en
  Adder #(.width(16)) adder_3 (.a(bit_extender_2_out), .b(subtractor_1_out), .out(adder_3_out));  // open: cin, cout
  Multiplexer #(.width(16)) multiplexer_5 (
    .in0(multiplexer_4_out), .in1(adder_3_out), .out(multiplexer_5_out), .sel(alu_control2_1_jump));  // open: en
  Multiplexer #(.width(16)) multiplexer_6 (
    .in0(multiplexer_5_out), .in1(register_2_q), .out(multiplexer_6_out), .sel(alu_control2_1_rtn));  // open: en
  and and_1 (and_1_out, id_ex_1_m_2[0], alu_1_ble_zero);
  Multiplexer #(.width(16)) multiplexer_7 (
    .in0(multiplexer_6_out), .in1({16{1'b0}}), .out(multiplexer_7_out), .sel(alu_control2_1_reboot));  // open: en
  or or_1 (Branch_Jump, and_1_out, alu_control2_1_jump);
  EX_MEM ex_mem_1 (
    .WB({exwrite, id_ex_1_wb_2[0]}), .M(id_ex_1_m_2[2:1]), .alu_result(alu_1_alu_result), .D(id_ex_1_r2_2),
    .w(ex), .WB_2({memwrite, ex_mem_1_wb_2[0]}), .M_2(ex_mem_1_m_2), .ALU_result_2(ex_mem_1_alu_result_2),
    .D_2(ex_mem_1_d_2), .w_2(mem), .clock(clock), .halt(id_ex_1_halt_2), .halt_2(ex_mem_1_halt_2),
    .raread(alu_control2_1_call), .raread_2(rread));  // open: reset
  RAM #(.addrWidth(16), .dataWidth(16), .bus("separate")) ram_1 (
    .addr(ex_mem_1_alu_result_2), .din(ex_mem_1_d_2), .data(ram_1_data), .str(ex_mem_1_m_2[1]), .clk(clock),
    .ld(ex_mem_1_m_2[0]));  // open: sel, clr
  MEM_WB mem_wb_1 (
    .WB({memwrite, ex_mem_1_wb_2[0]}), .alu_result(ex_mem_1_alu_result_2), .D(ram_1_data), .w(mem),
    .halt(ex_mem_1_halt_2), .WB_2({w, mem_wb_1_wb_2[0]}), .alu_result_2(mem_wb_1_alu_result_2),
    .D_2(mem_wb_1_d_2), .w_2(wreg), .halt_2(halt), .clock(clock));  // open: reset
  Multiplexer #(.width(16)) multiplexer_8 (
    .in0(mem_wb_1_alu_result_2), .in1(mem_wb_1_d_2), .out(multiplexer_8_out), .sel(mem_wb_1_wb_2[0]));  // open: en

  // Notes on the sheet:
  //   contents of rom_1 (hex, n*v repeats v):
  //   0 a 28 40 3200 2a60 b30 5b22 1334 9800 0 0 9800
endmodule

module Control_Unit (
  input  op15,
  input  op14,
  input  op13,
  input  op12,
  input  op11,
  output RegDst,
  output RegWrite,
  output ALUSrc,
  output Branch,
  output MemRead,
  output MemWrite,
  output MemToReg,
  output ALUop1,
  output ALUop2,
  output ALUop3,
  output ALUop4,
  output halt
);

  wire and_1_out, and_2_out, and_3_out, and_4_out, and_5_out, and_6_out, and_7_out, and_8_out, and_9_out,
       and_10_out, and_11_out, and_12_out, and_13_out, and_14_out, and_15_out, and_16_out, and_20_out,
       and_21_out, and_22_out, and_23_out, and_24_out, and_25_out, and_26_out, and_27_out, and_28_out,
       and_29_out, and_30_out, and_31_out, and_32_out, and_33_out, and_34_out, and_35_out, and_36_out,
       and_37_out, and_38_out, and_39_out, and_40_out, and_41_out, not_1_out, not_2_out, not_3_out,
       not_4_out, not_5_out, not_6_out, not_7_out, not_8_out, not_9_out, not_10_out, not_11_out, not_12_out,
       not_13_out, not_14_out, not_15_out, not_16_out, not_17_out, not_18_out, not_19_out, not_20_out,
       not_21_out, not_22_out, not_23_out, not_24_out, not_25_out, not_26_out, not_27_out, not_28_out,
       not_29_out, not_30_out, not_31_out, not_32_out, not_33_out, not_34_out, not_35_out, not_36_out,
       not_37_out, not_38_out, not_39_out, not_40_out, not_41_out, not_42_out, not_43_out, not_44_out,
       not_45_out, not_46_out, not_47_out, not_48_out, not_49_out, not_50_out, not_51_out, not_52_out,
       not_53_out, not_54_out, not_55_out, not_56_out, not_57_out, not_58_out, not_59_out, not_60_out,
       not_61_out, not_62_out, not_63_out, not_64_out, not_65_out, not_66_out, not_67_out, not_68_out,
       not_69_out, not_70_out, not_71_out;

  not not_1 (not_1_out, op15);
  not not_2 (not_2_out, op14);
  not not_3 (not_3_out, op13);
  not not_4 (not_4_out, op15);
  not not_5 (not_5_out, op14);
  not not_6 (not_6_out, op13);
  not not_7 (not_7_out, op12);
  not not_8 (not_8_out, op11);
  not not_9 (not_9_out, op15);
  not not_10 (not_10_out, op14);
  not not_11 (not_11_out, op13);
  not not_12 (not_12_out, op12);
  not not_13 (not_13_out, op14);
  not not_14 (not_14_out, op12);
  not not_15 (not_15_out, op11);
  not not_16 (not_16_out, op15);
  not not_17 (not_17_out, op14);
  not not_18 (not_18_out, op12);
  not not_19 (not_19_out, op11);
  not not_20 (not_20_out, op14);
  not not_21 (not_21_out, op13);
  not not_22 (not_22_out, op12);
  not not_23 (not_23_out, op13);
  not not_24 (not_24_out, op11);
  not not_25 (not_25_out, op13);
  not not_26 (not_26_out, op14);
  not not_27 (not_27_out, op12);
  not not_28 (not_28_out, op14);
  not not_29 (not_29_out, op11);
  not not_30 (not_30_out, op14);
  not not_31 (not_31_out, op12);
  not not_32 (not_32_out, op14);
  not not_33 (not_33_out, op13);
  not not_34 (not_34_out, op12);
  not not_35 (not_35_out, op11);
  not not_36 (not_36_out, op14);
  not not_37 (not_37_out, op13);
  not not_38 (not_38_out, op12);
  not not_39 (not_39_out, op11);
  not not_40 (not_40_out, op13);
  not not_41 (not_41_out, op12);
  not not_42 (not_42_out, op14);
  not not_43 (not_43_out, op13);
  not not_44 (not_44_out, op14);
  not not_45 (not_45_out, op13);
  not not_46 (not_46_out, op15);
  not not_47 (not_47_out, op14);
  not not_48 (not_48_out, op13);
  not not_49 (not_49_out, op14);
  not not_50 (not_50_out, op13);
  not not_51 (not_51_out, op12);
  not not_52 (not_52_out, op13);
  not not_53 (not_53_out, op11);
  not not_54 (not_54_out, op12);
  not not_55 (not_55_out, op15);
  not not_56 (not_56_out, op14);
  not not_57 (not_57_out, op13);
  not not_58 (not_58_out, op12);
  not not_59 (not_59_out, op11);
  not not_60 (not_60_out, op13);
  not not_61 (not_61_out, op12);
  not not_62 (not_62_out, op11);
  not not_63 (not_63_out, op15);
  not not_64 (not_64_out, op14);
  not not_65 (not_65_out, op13);
  not not_66 (not_66_out, op13);
  not not_67 (not_67_out, op12);
  not not_68 (not_68_out, op13);
  not not_69 (not_69_out, op12);
  not not_70 (not_70_out, op14);
  not not_71 (not_71_out, op13);
  and and_1 (and_1_out, not_1_out, not_2_out, not_3_out, op11);
  and and_2 (and_2_out, not_4_out, not_5_out, not_6_out, op12);
  and and_3 (and_3_out, op14, op13, not_7_out);
  and and_4 (and_4_out, op14, op13, not_8_out);
  and and_5 (and_5_out, op15, op14, op13);
  and and_6 (and_6_out, not_9_out, not_10_out, not_11_out);
  and and_7 (and_7_out, op13, not_12_out);
  and and_8 (and_8_out, not_13_out, op13, op11);
  and and_9 (and_9_out, op14, not_14_out);
  and and_10 (and_10_out, op14, not_15_out);
  and and_11 (and_11_out, not_16_out, not_17_out, not_18_out, not_19_out);
  and and_12 (and_12_out, not_20_out, op13);
  and and_13 (and_13_out, op14, not_21_out, not_22_out);
  and and_14 (and_14_out, op14, not_23_out, not_24_out);
  and and_15 (and_15_out, op14, not_25_out, op12, op11);
  and and_16 (and_16_out, op15, op14, op12, op11);
  and and_17 (MemRead, not_26_out, op13, not_27_out, op11);
  and and_18 (MemWrite, not_28_out, op13, op12, not_29_out);
  and and_19 (MemToReg, not_30_out, op13, not_31_out, op11);
  and and_20 (and_20_out, not_32_out, not_33_out, not_34_out, not_35_out);
  and and_21 (and_21_out, op14, op13, op12);
  and and_22 (and_22_out, op15, not_36_out, not_37_out);
  and and_23 (and_23_out, op13, not_38_out, not_39_out);
  and and_24 (and_24_out, op14, not_40_out, op12, op11);
  and and_25 (and_25_out, op14, op13, not_41_out);
  and and_26 (and_26_out, op15, not_42_out, not_43_out, op11);
  and and_27 (and_27_out, op15, not_44_out, not_45_out, op12);
  and and_28 (and_28_out, op15, op14, op13, op11);
  and and_29 (and_29_out, not_46_out, not_47_out, not_48_out, op12);
  and and_30 (and_30_out, not_49_out, not_50_out, op12, op11);
  and and_31 (and_31_out, op14, not_51_out, op11);
  and and_32 (and_32_out, op14, not_52_out, op12, not_53_out);
  and and_33 (and_33_out, op14, op13, not_54_out);
  and and_34 (and_34_out, not_55_out, op14, op13, op11);
  and and_35 (and_35_out, op15, not_56_out, not_57_out, not_58_out, not_59_out);
  and and_36 (and_36_out, not_60_out, not_61_out, not_62_out);
  and and_37 (and_37_out, not_63_out, not_64_out, not_65_out, op11);
  and and_38 (and_38_out, op14, not_66_out, op12);
  and and_39 (and_39_out, op14, op13, not_67_out, op11);
  and and_40 (and_40_out, op15, not_68_out, op12);
  and and_41 (and_41_out, op15, op13, not_69_out, op11);
  and and_42 (halt, op15, not_70_out, not_71_out, op12, op11);
  or or_1 (RegDst, and_1_out, and_2_out, and_3_out, and_4_out, and_5_out);
  or or_2 (RegWrite, and_6_out, and_7_out, and_8_out, and_9_out, and_10_out);
  or or_3 (ALUSrc, and_11_out, and_12_out, and_13_out, and_14_out);
  or or_4 (Branch, and_15_out, and_16_out);
  or or_5 (ALUop1, and_20_out, and_21_out, and_22_out);
  or or_6 (ALUop2, and_23_out, and_24_out, and_25_out, and_26_out, and_27_out, and_28_out);
  or or_7 (ALUop3, and_29_out, and_30_out, and_31_out, and_32_out, and_33_out, and_34_out, and_35_out);
  or or_8 (ALUop4, and_36_out, and_37_out, and_38_out, and_39_out, and_40_out, and_41_out);
endmodule

// Register File
module registerfile (
  input  write,
  input  [2:0] read_register_1,
  input  [2:0] write_Register,
  input  [2:0] read_register_2,
  input  clock,
  input  [15:0] write_data,
  output [15:0] data1,
  output [15:0] data2
);

  wire and_1_out, and_2_out, and_3_out, and_4_out, and_5_out, and_6_out, and_7_out, and_8_out,
       decoder_1_out0, decoder_1_out1, decoder_1_out2, decoder_1_out3, decoder_1_out4, decoder_1_out5,
       decoder_1_out6, decoder_1_out7;
  wire [15:0] register_1_q, register_2_q, register_3_q, register_4_q, register_5_q, register_6_q,
       register_7_q, register_8_q;

  Decoder #(.select(3)) decoder_1 (
    .out0(decoder_1_out0), .out1(decoder_1_out1), .out2(decoder_1_out2), .out3(decoder_1_out3),
    .out4(decoder_1_out4), .out5(decoder_1_out5), .out6(decoder_1_out6), .out7(decoder_1_out7),
    .sel(write_Register));  // open: en
  and and_1 (and_1_out, write, decoder_1_out0);
  and and_2 (and_2_out, write, decoder_1_out1);
  and and_3 (and_3_out, write, decoder_1_out2);
  and and_4 (and_4_out, write, decoder_1_out3);
  and and_5 (and_5_out, decoder_1_out4, write);
  and and_6 (and_6_out, decoder_1_out5, write);
  and and_7 (and_7_out, decoder_1_out6, write);
  and and_8 (and_8_out, decoder_1_out7, write);
  Register #(.width(16)) register_1 (.D(write_data), .en(and_1_out), .Q(register_1_q), .clk(clock));  // open: clr
  Register #(.width(16)) register_2 (.D(write_data), .en(and_2_out), .Q(register_2_q), .clk(clock));  // open: clr
  Register #(.width(16)) register_3 (.D(write_data), .en(and_3_out), .Q(register_3_q), .clk(clock));  // open: clr
  Register #(.width(16)) register_4 (.D(write_data), .en(and_4_out), .Q(register_4_q), .clk(clock));  // open: clr
  Register #(.width(16)) register_5 (.D(write_data), .en(and_5_out), .Q(register_5_q), .clk(clock));  // open: clr
  Register #(.width(16)) register_6 (.D(write_data), .en(and_6_out), .Q(register_6_q), .clk(clock));  // open: clr
  Register #(.width(16)) register_7 (.D(write_data), .en(and_7_out), .Q(register_7_q), .clk(clock));  // open: clr
  Register #(.width(16)) register_8 (.D(write_data), .en(and_8_out), .Q(register_8_q), .clk(clock));  // open: clr
  Multiplexer #(.select(3), .width(16)) multiplexer_1 (
    .in0(register_1_q), .in1(register_2_q), .in2(register_3_q), .in3(register_4_q), .in4(register_5_q),
    .in5(register_6_q), .in6(register_7_q), .in7(register_8_q), .out(data1), .sel(read_register_1));  // open: en
  Multiplexer #(.select(3), .width(16)) multiplexer_2 (
    .in0(register_1_q), .in1(register_2_q), .in2(register_3_q), .in3(register_4_q), .in4(register_5_q),
    .in5(register_6_q), .in6(register_7_q), .in7(register_8_q), .out(data2), .sel(read_register_2));  // open: en
endmodule

module ALU_Control (
  input  ALUop1,
  input  ALUop2,
  input  ALUop3,
  input  ALUop4,
  output [3:0] out_5,
  output [3:0] ALU_control_output
);

  wire [3:0] adder_1_out, adder_2_out, bit_extender_2_out, bit_extender_3_out, bit_extender_4_out,
       shifter_1_out, shifter_2_out, shifter_3_out;

  assign out_5 = {{3{1'b0}}, ALUop1};  // Bit_Extender bit_extender_1
  assign bit_extender_2_out = {{3{1'b0}}, ALUop2};  // Bit_Extender bit_extender_2
  assign bit_extender_3_out = {{3{1'b0}}, ALUop3};  // Bit_Extender bit_extender_3
  Shifter #(.width(4)) shifter_1 (.in(out_5), .\dist (2'b11), .out(shifter_1_out));
  Shifter #(.width(4)) shifter_2 (.in(bit_extender_2_out), .\dist (2'b10), .out(shifter_2_out));
  Shifter #(.width(4)) shifter_3 (.in(bit_extender_3_out), .\dist (2'b01), .out(shifter_3_out));
  assign bit_extender_4_out = {{3{1'b0}}, ALUop4};  // Bit_Extender bit_extender_4
  Adder #(.width(4)) adder_1 (.a(shifter_1_out), .b(shifter_2_out), .out(adder_1_out));  // open: cin, cout
  Adder #(.width(4)) adder_2 (.a(shifter_3_out), .b(bit_extender_4_out), .out(adder_2_out));  // open: cin, cout
  Adder #(.width(4)) adder_3 (.a(adder_1_out), .b(adder_2_out), .out(ALU_control_output));  // open: cin, cout
endmodule

module ALU (
  input  [15:0] Data1,
  input  [15:0] Data2,
  input  [3:0] ALU_sel,
  output [15:0] _0000data1self,
  output [15:0] _0001plus,
  output [15:0] _0010and,
  output [15:0] _0011or,
  output [15:0] _0100negdata1,
  output [15:0] SLT0110,
  output [15:0] shiftleft0111,
  output [15:0] shiftright1000,
  output [15:0] _1001,
  output [15:0] ALU_result,
  output BLE_ZERO,
  output [15:0] out_15
);

  wire comparator_1_gt, comparator_2_lt;
  wire [3:0] bitselector_1_out, bitselector_2_out;
  wire [15:0] adder_1_out, and_1_out, bit_extender_1_out, negator_1_out, or_1_out, shifter_1_out,
       shifter_2_out;

  BitSelector #(.width(16), .group(4)) bitselector_1 (.in(Data2), .out(bitselector_1_out), .sel(2'b00));
  Comparator #(.width(16), .mode("unsigned")) comparator_1 (
    .a(Data2), .b(Data1), .gt(comparator_1_gt));  // open: eq, lt
  Comparator #(.width(16), .mode("unsigned")) comparator_2 (
    .a(Data1), .b(Data2), .lt(comparator_2_lt));  // open: gt, eq
  BitSelector #(.width(16), .group(4)) bitselector_2 (.in(Data2), .out(bitselector_2_out), .sel(2'b00));
  Adder #(.width(16)) adder_1 (.a(Data1), .b(Data2), .out(adder_1_out));  // open: cin, cout
  assign or_1_out = Data1 | Data2;  // OR_Gate or_1, 16 bits wide
  Negator #(.width(16)) negator_1 (.in(Data1), .out(negator_1_out));
  not not_1 (BLE_ZERO, comparator_1_gt);
  assign bit_extender_1_out = {{15{1'b0}}, comparator_2_lt};  // Bit_Extender bit_extender_1
  assign and_1_out = Data1 & Data2;  // AND_Gate and_1, 16 bits wide
  Shifter #(.width(16)) shifter_1 (.in(Data1), .\dist (bitselector_1_out), .out(shifter_1_out));
  Shifter #(.width(16), .shift("lr")) shifter_2 (.in(Data1), .\dist (bitselector_2_out), .out(shifter_2_out));
  Adder #(.width(16)) adder_2 (.a(bit_extender_1_out), .b({16{1'b0}}), .out(out_15));  // open: cin, cout
  Multiplexer #(.select(4), .width(16)) multiplexer_1 (
    .in0(Data1), .in1(adder_1_out), .in2(and_1_out), .in3(or_1_out), .in4(negator_1_out), .in6(out_15),
    .in7(shifter_1_out), .in8(shifter_2_out), .in9(Data2), .out(ALU_result), .sel(ALU_sel));  // open: in5, in10, in11, in12, in13, in14, in15, en
endmodule

module canvas (
  input  [15:0] in_1,
  input  [3:0] in_2,
  input  [3:0] in_3,
  input  [15:0] in_4,
  input  in_5,
  input  [15:0] in_6,
  input  [15:0] in_7,
  input  [3:0] in_8,
  input  [15:0] in_9,
  input  [7:0] in_10,
  input  [7:0] in_11,
  input  in_12,
  input  in_13,
  input  [4:0] in_14,
  output [15:0] out_15,
  output [15:0] out_16,
  output [15:0] out_17,
  output [15:0] out_18,
  output [15:0] out_19
);

  wire not_1_out;

  Register #(.width(16)) register_1 ();  // open: D, en, Q, clk, clr
  Shifter #(.width(16)) shifter_1 (.in(out_15), .\dist (in_2), .out(out_16));
  Shifter #(.width(16), .shift("lr")) shifter_2 (.in(out_15), .\dist (in_3), .out(out_17));
  Negator #(.width(16)) negator_1 (.in(in_1), .out(out_15));
  Adder adder_1 (.a(in_10), .b(in_11));  // open: out, cin, cout
  assign out_19 = {{11{in_14[4]}}, in_14};  // Bit_Extender bit_extender_1
  ALU alu_1 (
    .Data1(in_4), .Data2(in_6), .ALU_sel(in_8));  // open: _0000data1self, _0001plus, _0010and, _0011or, _0100negdata1, SLT0110, shiftleft0111, shiftright1000, _1001, ALU_result, BLE_ZERO, out_15
  RAM ram_1 (.sel(in_5));  // open: addr, data, clk, ld, clr
  RAM #(.addrWidth(16), .dataWidth(16)) ram_2 (.addr(in_9), .data(out_18), .clk(in_12), .ld(in_13));  // open: sel, clr
  Multiplexer #(.width(16)) multiplexer_1 (.in1(in_7), .out(out_18), .sel(1'b1), .en(not_1_out));  // open: in0
  not not_1 (not_1_out, in_13);
endmodule

module ALU_Control2 (
  input  ALUop1,
  input  ALUop2,
  input  ALUop3,
  input  ALUop4,
  output jump,
  output call,
  output rtn,
  output reboot
);

  wire not_1_out, not_2_out, not_3_out, not_4_out, not_5_out;

  not not_1 (not_1_out, ALUop2);
  and and_1 (jump, ALUop1, not_1_out, ALUop3);
  not not_2 (not_2_out, ALUop2);
  not not_3 (not_3_out, ALUop3);
  not not_4 (not_4_out, ALUop4);
  not not_5 (not_5_out, ALUop3);
  and and_2 (call, ALUop1, not_2_out, ALUop3, ALUop4);
  and and_3 (rtn, ALUop1, ALUop2, not_3_out, not_4_out);
  and and_4 (reboot, ALUop1, ALUop2, not_5_out, ALUop4);
endmodule

module pipeline (
);

  wire alu_1_ble_zero, alu_control2_1_call, alu_control2_1_jump, alu_control2_1_reboot, alu_control2_1_rtn,
       and_1_out, Branch_Jump, clock, clock_1_out, control_unit_1_halt, control_unit_1_regdst,
       ex_mem_1_halt_2, exwrite, hazard_flushid, hazard_flushif, hazard_stallid, hazard_stallif,
       id_ex_1_halt_2, live, memwrite, not_1_out, regread_1_r1, regread_1_r2, rread, w;
  wire [0:0] ex_mem_1_m_2, id_ex_1_wb_2, mem_wb_1_wb_2;
  wire [1:0] control_unit_1_memtoreg, ex_mem_1_wb_2;
  wire [2:0] control_unit_1_branch, ex, id_ex_1_m_2, mem, multiplexer_2_out, wreg;
  wire [3:0] alu_control_1_alu_control_output;
  wire [4:0] control_unit_1_aluop1, id_ex_1_ex_2;
  wire [15:0] adder_1_out, adder_2_out, adder_3_out, alu_1_alu_result, bit_extender_1_out,
       bit_extender_2_out, ex_mem_1_alu_result_2, ex_mem_1_d_2, id_ex_1_imm_2, id_ex_1_pc_1_2, id_ex_1_r1_2,
       id_ex_1_r2_2, if_id_1_instru_2, if_id_1_pc_1_2, mem_wb_1_alu_result_2, mem_wb_1_d_2,
       multiplexer_3_out, multiplexer_4_out, multiplexer_5_out, multiplexer_6_out, multiplexer_7_out,
       multiplexer_8_out, ram_1_data, register_1_q, register_2_q, registerfile_1_data1, registerfile_1_data2,
       rom_1_data, subtractor_1_out;

  Register #(.width(16)) register_1 (
    .D(multiplexer_7_out), .en(hazard_stallif), .Q(register_1_q), .clk(clock));  // open: clr
  Adder #(.width(16)) adder_1 (.a(register_1_q), .b(16'h1), .out(adder_1_out));  // open: cin, cout
  ROM #(.addrWidth(16), .dataWidth(16)) rom_1 (.addr(register_1_q), .data(rom_1_data));  // open: sel
  Clock clock_1 (.out(clock_1_out));
  not not_1 (not_1_out, live);
  IF_ID if_id_1 (
    .PC_1(adder_1_out), .Instru(rom_1_data), .Enable(hazard_stallid), .PC_1_2(if_id_1_pc_1_2),
    .Instru_2(if_id_1_instru_2), .clock(clock), .reset(hazard_flushif));
  Multiplexer #(.enable("false")) multiplexer_1 (.in0(clock_1_out), .in1(1'b0), .out(clock), .sel(not_1_out));
  hazard hazard (
    .r1read(regread_1_r1), .ex(ex), .exwrite(exwrite), .r2(if_id_1_instru_2[7:5]),
    .r1(if_id_1_instru_2[10:8]), .mem(mem), .memwrite(memwrite), .branch___jump(Branch_Jump), .wreg(wreg),
    .W(w), .flushID(hazard_flushid), .r2read(regread_1_r2), .stallIF(hazard_stallif),
    .stallID(hazard_stallid), .flushIF(hazard_flushif));  // open: in_1
  regread regread_1 (
    .op1(if_id_1_instru_2[15]), .op2(if_id_1_instru_2[14]), .op3(if_id_1_instru_2[13]),
    .op4(if_id_1_instru_2[12]), .op5(if_id_1_instru_2[11]), .r1(regread_1_r1), .r2(regread_1_r2));
  Control_Unit control_unit_1 (
    .op15(if_id_1_instru_2[15]), .op14(if_id_1_instru_2[14]), .op13(if_id_1_instru_2[13]),
    .op12(if_id_1_instru_2[12]), .op11(if_id_1_instru_2[11]), .RegDst(control_unit_1_regdst),
    .RegWrite(control_unit_1_memtoreg[1]), .ALUSrc(control_unit_1_aluop1[4]),
    .Branch(control_unit_1_branch[0]), .MemRead(control_unit_1_branch[1]),
    .MemWrite(control_unit_1_branch[2]), .MemToReg(control_unit_1_memtoreg[0]),
    .ALUop1(control_unit_1_aluop1[0]), .ALUop2(control_unit_1_aluop1[1]), .ALUop3(control_unit_1_aluop1[2]),
    .ALUop4(control_unit_1_aluop1[3]), .halt(control_unit_1_halt));
  Multiplexer #(.width(3)) multiplexer_2 (
    .in0(if_id_1_instru_2[7:5]), .in1(if_id_1_instru_2[4:2]), .out(multiplexer_2_out),
    .sel(control_unit_1_regdst));  // open: en
  assign bit_extender_1_out = {{11{if_id_1_instru_2[4]}}, if_id_1_instru_2[4:0]};  // Bit_Extender bit_extender_1
  assign bit_extender_2_out = {{5{if_id_1_instru_2[10]}}, if_id_1_instru_2[10:0]};  // Bit_Extender bit_extender_2
  registerfile registerfile_1 (
    .write(w), .read_register_1(if_id_1_instru_2[10:8]), .write_Register(wreg),
    .read_register_2(if_id_1_instru_2[7:5]), .clock(clock), .write_data(multiplexer_8_out),
    .data1(registerfile_1_data1), .data2(registerfile_1_data2));
  ID___EX id_ex_1 (
    .WB(control_unit_1_memtoreg), .M(control_unit_1_branch), .EX(control_unit_1_aluop1),
    .PC_1(if_id_1_pc_1_2), .r1(registerfile_1_data1), .r2(registerfile_1_data2), .w(multiplexer_2_out),
    .imm(bit_extender_1_out), .WB_2({exwrite, id_ex_1_wb_2[0]}), .M_2(id_ex_1_m_2), .EX_2(id_ex_1_ex_2),
    .PC_1_2(id_ex_1_pc_1_2), .r1_2(id_ex_1_r1_2), .r2_2(id_ex_1_r2_2), .w_2(ex), .imm_2(id_ex_1_imm_2),
    .clock(clock), .reset(hazard_flushid), .halt(control_unit_1_halt), .halt_2(id_ex_1_halt_2));
  Subtractor #(.width(16)) subtractor_1 (.a(id_ex_1_pc_1_2), .b(16'h1), .out(subtractor_1_out));  // open: bin, bout
  Multiplexer #(.width(16)) multiplexer_3 (
    .in0(id_ex_1_r2_2), .in1(id_ex_1_imm_2), .out(multiplexer_3_out), .sel(id_ex_1_ex_2[4]));  // open: en
  Register #(.width(16)) register_2 (.D(adder_1_out), .en(rread), .Q(register_2_q), .clk(clock));  // open: clr
  Adder #(.width(16)) adder_2 (.a(subtractor_1_out), .b(id_ex_1_imm_2), .out(adder_2_out));  // open: cin, cout
  ALU alu_1 (
    .Data1(id_ex_1_r1_2), .Data2(multiplexer_3_out), .ALU_sel(alu_control_1_alu_control_output),
    .ALU_result(alu_1_alu_result), .BLE_ZERO(alu_1_ble_zero));  // open: _0000data1self, _0001plus, _0010and, _0011or, _0100negdata1, SLT0110, shiftleft0111, shiftright1000, _1001, out_15
  ALU_Control alu_control_1 (
    .ALUop1(id_ex_1_ex_2[0]), .ALUop2(id_ex_1_ex_2[1]), .ALUop3(id_ex_1_ex_2[2]), .ALUop4(id_ex_1_ex_2[3]),
    .ALU_control_output(alu_control_1_alu_control_output));  // open: out_5
  ALU_Control2 alu_control2_1 (
    .ALUop1(id_ex_1_ex_2[0]), .ALUop2(id_ex_1_ex_2[1]), .ALUop3(id_ex_1_ex_2[2]), .ALUop4(id_ex_1_ex_2[3]),
    .jump(alu_control2_1_jump), .call(alu_control2_1_call), .rtn(alu_control2_1_rtn),
    .reboot(alu_control2_1_reboot));
  Multiplexer #(.width(16)) multiplexer_4 (
    .in0(id_ex_1_pc_1_2), .in1(adder_2_out), .out(multiplexer_4_out), .sel(and_1_out));  // open: en
  Adder #(.width(16)) adder_3 (.a(bit_extender_2_out), .b(subtractor_1_out), .out(adder_3_out));  // open: cin, cout
  Multiplexer #(.width(16)) multiplexer_5 (
    .in0(multiplexer_4_out), .in1(adder_3_out), .out(multiplexer_5_out), .sel(alu_control2_1_jump));  // open: en
  Multiplexer #(.width(16)) multiplexer_6 (
    .in0(multiplexer_5_out), .in1(register_2_q), .out(multiplexer_6_out), .sel(alu_control2_1_rtn));  // open: en
  and and_1 (and_1_out, id_ex_1_m_2[0], alu_1_ble_zero);
  Multiplexer #(.width(16)) multiplexer_7 (
    .in0(multiplexer_6_out), .in1({16{1'b0}}), .out(multiplexer_7_out), .sel(alu_control2_1_reboot));  // open: en
  or or_1 (Branch_Jump, and_1_out, alu_control2_1_jump);
  EX_MEM ex_mem_1 (
    .WB({exwrite, id_ex_1_wb_2[0]}), .M(id_ex_1_m_2[2:1]), .alu_result(alu_1_alu_result),
    .D(multiplexer_3_out), .w(ex), .WB_2(ex_mem_1_wb_2), .M_2({memwrite, ex_mem_1_m_2[0]}),
    .ALU_result_2(ex_mem_1_alu_result_2), .D_2(ex_mem_1_d_2), .w_2(mem), .clock(clock),
    .halt(id_ex_1_halt_2), .halt_2(ex_mem_1_halt_2), .raread(alu_control2_1_call), .raread_2(rread));  // open: reset
  RAM #(.addrWidth(16), .dataWidth(16), .bus("separate")) ram_1 (
    .addr(ex_mem_1_alu_result_2), .din(ex_mem_1_d_2), .data(ram_1_data), .str(memwrite), .clk(clock),
    .ld(ex_mem_1_m_2[0]));  // open: sel, clr
  MEM_WB mem_wb_1 (
    .WB(ex_mem_1_wb_2), .alu_result(ex_mem_1_alu_result_2), .D(ram_1_data), .w(mem), .halt(ex_mem_1_halt_2),
    .WB_2({w, mem_wb_1_wb_2[0]}), .alu_result_2(mem_wb_1_alu_result_2), .D_2(mem_wb_1_d_2), .w_2(wreg),
    .halt_2(live), .clock(clock));  // open: reset
  Multiplexer #(.width(16)) multiplexer_8 (
    .in0(mem_wb_1_alu_result_2), .in1(mem_wb_1_d_2), .out(multiplexer_8_out), .sel(mem_wb_1_wb_2[0]));  // open: en

  // Notes on the sheet:
  //   contents of rom_1 (hex, n*v repeats v):
  //   6 6 24 8007 3a60 7 28 8003 3a80 7803 828 8800 9800
endmodule

module IF_ID (
  input  [15:0] PC_1,
  input  [15:0] Instru,
  input  Enable,
  input  reset,
  input  clock,
  output [15:0] PC_1_2,
  output [15:0] Instru_2
);

  Register #(.width(16)) register_1 (.D(PC_1), .en(Enable), .Q(PC_1_2), .clk(clock), .clr(reset));
  Register #(.width(16)) register_2 (.D(Instru), .en(Enable), .Q(Instru_2), .clk(clock), .clr(reset));
endmodule

// ID/EX
module ID___EX (
  input  [1:0] WB,
  input  [2:0] M,
  input  [4:0] EX,
  input  [15:0] PC_1,
  input  [15:0] r1,
  input  [15:0] r2,
  input  [2:0] w,
  input  [15:0] imm,
  input  halt,
  input  clock,
  input  reset,
  output [1:0] WB_2,
  output [2:0] M_2,
  output [4:0] EX_2,
  output [15:0] PC_1_2,
  output [15:0] r1_2,
  output [15:0] r2_2,
  output [2:0] w_2,
  output [15:0] imm_2,
  output halt_2
);

  Register #(.width(2)) register_1 (.D(WB), .en(1'b1), .Q(WB_2), .clk(clock), .clr(reset));
  Register #(.width(3)) register_2 (.D(M), .en(1'b1), .Q(M_2), .clk(clock), .clr(reset));
  Register #(.width(5)) register_3 (.D(EX), .en(1'b1), .Q(EX_2), .clk(clock), .clr(reset));
  Register #(.width(16)) register_4 (.D(PC_1), .en(1'b1), .Q(PC_1_2), .clk(clock), .clr(reset));
  Register #(.width(16)) register_5 (.D(r1), .en(1'b1), .Q(r1_2), .clk(clock), .clr(reset));
  Register #(.width(16)) register_6 (.D(r2), .en(1'b1), .Q(r2_2), .clk(clock), .clr(reset));
  Register #(.width(3)) register_7 (.D(w), .en(1'b1), .Q(w_2), .clk(clock), .clr(reset));
  Register #(.width(16)) register_8 (.D(imm), .en(1'b1), .Q(imm_2), .clk(clock), .clr(reset));
  Register #(.width(1)) register_9 (.D(halt), .en(1'b1), .Q(halt_2), .clk(clock), .clr(reset));
endmodule

module EX_MEM (
  input  [1:0] WB,
  input  [1:0] M,
  input  [15:0] alu_result,
  input  [15:0] D,
  input  [2:0] w,
  input  halt,
  input  raread,
  input  clock,
  input  reset,
  output [1:0] WB_2,
  output [1:0] M_2,
  output [15:0] ALU_result_2,
  output [15:0] D_2,
  output [2:0] w_2,
  output halt_2,
  output raread_2
);

  Register #(.width(2)) register_1 (.D(WB), .en(1'b1), .Q(WB_2), .clk(clock), .clr(reset));
  Register #(.width(2)) register_2 (.D(M), .en(1'b1), .Q(M_2), .clk(clock), .clr(reset));
  Register #(.width(16)) register_3 (.D(alu_result), .en(1'b1), .Q(ALU_result_2), .clk(clock), .clr(reset));
  Register #(.width(16)) register_4 (.D(D), .en(1'b1), .Q(D_2), .clk(clock), .clr(reset));
  Register #(.width(3)) register_5 (.D(w), .en(1'b1), .Q(w_2), .clk(clock), .clr(reset));
  Register #(.width(1)) register_6 (.D(halt), .en(1'b1), .Q(halt_2), .clk(clock), .clr(reset));
  Register #(.width(1)) register_7 (.D(raread), .en(1'b1), .Q(raread_2), .clk(clock), .clr(reset));
endmodule

module MEM_WB (
  input  [1:0] WB,
  input  [15:0] alu_result,
  input  [15:0] D,
  input  [2:0] w,
  input  halt,
  input  clock,
  input  reset,
  output [1:0] WB_2,
  output [15:0] alu_result_2,
  output [15:0] D_2,
  output [2:0] w_2,
  output halt_2
);

  Register #(.width(2)) register_1 (.D(WB), .en(1'b1), .Q(WB_2), .clk(clock), .clr(reset));
  Register #(.width(16)) register_2 (.D(alu_result), .en(1'b1), .Q(alu_result_2), .clk(clock), .clr(reset));
  Register #(.width(16)) register_3 (.D(D), .en(1'b1), .Q(D_2), .clk(clock), .clr(reset));
  Register #(.width(3)) register_4 (.D(w), .en(1'b1), .Q(w_2), .clk(clock), .clr(reset));
  Register #(.width(1)) register_5 (.D(halt), .en(1'b1), .Q(halt_2), .clk(clock), .clr(reset));
endmodule

module regread (
  input  op1,
  input  op2,
  input  op3,
  input  op4,
  input  op5,
  output r1,
  output r2
);

  wire and_1_out, and_2_out, and_3_out, and_4_out, and_5_out, and_6_out, and_7_out, and_8_out, and_9_out,
       and_10_out, not_1_out, not_2_out, not_3_out, not_4_out, not_5_out, not_6_out, not_7_out, not_8_out,
       not_9_out, not_10_out, not_11_out, not_12_out, not_13_out, not_14_out, not_15_out, not_16_out,
       not_17_out, not_18_out;

  not not_1 (not_1_out, op1);
  not not_2 (not_2_out, op2);
  not not_3 (not_3_out, op1);
  not not_4 (not_4_out, op2);
  not not_5 (not_5_out, op2);
  not not_6 (not_6_out, op3);
  not not_7 (not_7_out, op4);
  not not_8 (not_8_out, op5);
  not not_9 (not_9_out, op1);
  not not_10 (not_10_out, op2);
  not not_11 (not_11_out, op3);
  not not_12 (not_12_out, op1);
  not not_13 (not_13_out, op2);
  not not_14 (not_14_out, op5);
  not not_15 (not_15_out, op1);
  not not_16 (not_16_out, op4);
  not not_17 (not_17_out, op1);
  not not_18 (not_18_out, op5);
  and and_1 (and_1_out, not_1_out, not_2_out, op5);
  and and_2 (and_2_out, not_3_out, not_4_out, op4);
  and and_3 (and_3_out, not_5_out, op3);
  and and_4 (and_4_out, op2, not_6_out);
  and and_5 (and_5_out, op2, not_7_out);
  and and_6 (and_6_out, op2, not_8_out);
  and and_7 (and_7_out, not_9_out, not_10_out, not_11_out, op5);
  and and_8 (and_8_out, not_12_out, not_13_out, op4, not_14_out);
  and and_9 (and_9_out, not_15_out, op2, op3, not_16_out);
  and and_10 (and_10_out, not_17_out, op2, op3, not_18_out);
  or or_1 (r1, and_1_out, and_2_out, and_3_out, and_4_out, and_5_out, and_6_out);
  or or_2 (r2, and_7_out, and_8_out, and_9_out, and_10_out);
endmodule

module hazard (
  input  in_1,
  input  r1read,
  input  r2read,
  input  [2:0] ex,
  input  exwrite,
  input  [2:0] r2,
  input  [2:0] r1,
  input  [2:0] mem,
  input  memwrite,
  input  branch___jump,
  input  [2:0] wreg,
  input  W,
  output flushID,
  output stallIF,
  output stallID,
  output flushIF
);

  wire and_1_out, and_2_out, and_3_out, and_4_out, and_5_out, and_6_out, and_7_out, and_8_out, and_9_out,
       comparator_1_eq, comparator_2_eq, comparator_3_eq, comparator_4_eq, comparator_5_eq, comparator_6_eq,
       d_ff_1_q, d_ff_2_q, or_1_out, or_2_out, or_3_out, or_4_out;

  Comparator #(.width(3)) comparator_1 (.a(ex), .b(r2), .eq(comparator_1_eq));  // open: gt, lt
  Comparator #(.width(3)) comparator_2 (.a(ex), .b(r1), .eq(comparator_2_eq));  // open: gt, lt
  Comparator #(.width(3)) comparator_3 (.a(mem), .b(r2), .eq(comparator_3_eq));  // open: gt, lt
  Comparator #(.width(3)) comparator_4 (.a(mem), .b(r1), .eq(comparator_4_eq));  // open: gt, lt
  Comparator #(.width(3)) comparator_5 (.a(wreg), .b(r2), .eq(comparator_5_eq));  // open: gt, lt
  Comparator #(.width(3)) comparator_6 (.a(wreg), .b(r1), .eq(comparator_6_eq));  // open: gt, lt
  and and_1 (and_1_out, comparator_1_eq, r2read);
  and and_2 (and_2_out, comparator_2_eq, r1read);
  and and_3 (and_3_out, comparator_3_eq, r2read);
  and and_4 (and_4_out, comparator_4_eq, r1read);
  and and_5 (and_5_out, comparator_5_eq, r2read);
  and and_6 (and_6_out, comparator_6_eq, r1read);
  or or_1 (or_1_out, and_1_out, and_2_out);
  or or_2 (or_2_out, and_3_out, and_4_out);
  or or_3 (or_3_out, and_5_out, and_6_out);
  and and_7 (and_7_out, exwrite, or_1_out);
  or or_4 (or_4_out, and_7_out, and_8_out, and_9_out);
  and and_8 (and_8_out, memwrite, or_2_out);
  and and_9 (and_9_out, W, or_3_out);
  D_Flip_Flop #(.trigger("falling")) d_ff_1 (.clk(in_1), .D(or_4_out), .Q(d_ff_1_q));  // open: Qn, preset, en, reset
  not not_1 (stallIF, or_4_out);
  not not_2 (stallID, or_4_out);
  and and_10 (flushID, in_1, d_ff_1_q);
  D_Flip_Flop #(.trigger("falling")) d_ff_2 (
    .clk(in_1), .D(branch___jump), .Q(d_ff_2_q));  // open: Qn, preset, en, reset
  and and_11 (flushIF, ~in_1, d_ff_2_q);  // AND_Gate

  // Other names for the same wires on the sheet: clock = in_1
endmodule

module pipelinefix (
  output [15:0] out_1,
  output [15:0] out_2,
  output [15:0] out_3,
  output [15:0] out_4,
  output [15:0] out_5,
  output [15:0] out_6,
  output [2:0] out_7,
  output [2:0] out_8,
  output [2:0] out_9,
  output [2:0] out_10,
  output [2:0] out_11
);

  wire alu_1_ble_zero, alu_control2_1_call, alu_control2_1_jump, alu_control2_1_reboot, alu_control2_1_rtn,
       and_1_out, Branch_Jump, clock, clock_1_out, control_unit_1_halt, control_unit_1_regdst,
       ex_mem_1_halt_2, exwrite, halt, hazard_flushid, hazard_flushif, hazard_stallid, hazard_stallif,
       id_ex_1_halt_2, memwrite, regread_1_r1, regread_1_r2, rread, w;
  wire [0:0] ex_mem_1_wb_2, id_ex_1_wb_2, mem_wb_1_wb_2;
  wire [1:0] control_unit_1_memtoreg, ex_mem_1_m_2;
  wire [2:0] control_unit_1_branch, id_ex_1_m_2, multiplexer_1_out;
  wire [3:0] alu_control_1_alu_control_output;
  wire [4:0] control_unit_1_aluop1, id_ex_1_ex_2;
  wire [15:0] adder_2_out, adder_3_out, alu_1_alu_result, bit_extender_1_out, bit_extender_2_out,
       ex_mem_1_alu_result_2, ex_mem_1_d_2, id_ex_1_imm_2, id_ex_1_r1_2, id_ex_1_r2_2, mem_wb_1_alu_result_2,
       mem_wb_1_d_2, multiplexer_3_out, multiplexer_4_out, multiplexer_5_out, multiplexer_6_out,
       multiplexer_8_out, ram_1_data, register_1_q, register_2_q, registerfile_1_data1, registerfile_1_data2,
       subtractor_1_out;

  Register #(.width(16)) register_1 (.D(out_1), .en(hazard_stallif), .Q(register_1_q), .clk(clock));  // open: clr
  Adder #(.width(16)) adder_1 (.a(register_1_q), .b(16'h1), .out(out_4));  // open: cin, cout
  ROM #(.addrWidth(16), .dataWidth(16)) rom_1 (.addr(register_1_q), .data(out_3));  // open: sel
  IF_ID if_id_1 (
    .PC_1(out_4), .Instru(out_3), .Enable(hazard_stallid), .PC_1_2(out_5), .Instru_2(out_6), .clock(clock),
    .reset(hazard_flushif));
  hazard hazard (
    .r1read(regread_1_r1), .ex(out_9), .exwrite(exwrite), .r2(out_6[7:5]), .r1(out_6[10:8]), .mem(out_11),
    .memwrite(memwrite), .branch___jump(Branch_Jump), .wreg(out_7), .W(w), .flushID(hazard_flushid),
    .r2read(regread_1_r2), .stallIF(hazard_stallif), .stallID(hazard_stallid), .flushIF(hazard_flushif));  // open: in_1
  regread regread_1 (
    .op1(out_6[15]), .op2(out_6[14]), .op3(out_6[13]), .op4(out_6[12]), .op5(out_6[11]), .r1(regread_1_r1),
    .r2(regread_1_r2));
  Control_Unit control_unit_1 (
    .op15(out_6[15]), .op14(out_6[14]), .op13(out_6[13]), .op12(out_6[12]), .op11(out_6[11]),
    .RegDst(control_unit_1_regdst), .RegWrite(control_unit_1_memtoreg[1]), .ALUSrc(control_unit_1_aluop1[4]),
    .Branch(control_unit_1_branch[0]), .MemRead(control_unit_1_branch[1]),
    .MemWrite(control_unit_1_branch[2]), .MemToReg(control_unit_1_memtoreg[0]),
    .ALUop1(control_unit_1_aluop1[0]), .ALUop2(control_unit_1_aluop1[1]), .ALUop3(control_unit_1_aluop1[2]),
    .ALUop4(control_unit_1_aluop1[3]), .halt(control_unit_1_halt));
  Multiplexer #(.width(3)) multiplexer_1 (
    .in0(out_6[7:5]), .in1(out_6[4:2]), .out(multiplexer_1_out), .sel(control_unit_1_regdst));  // open: en
  assign bit_extender_1_out = {{11{out_6[4]}}, out_6[4:0]};  // Bit_Extender bit_extender_1
  assign bit_extender_2_out = {{5{out_6[10]}}, out_6[10:0]};  // Bit_Extender bit_extender_2
  registerfile registerfile_1 (
    .write(w), .read_register_1(out_6[10:8]), .write_Register(out_7), .read_register_2(out_6[7:5]),
    .clock(clock), .write_data(multiplexer_8_out), .data1(registerfile_1_data1), .data2(registerfile_1_data2));
  Clock clock_1 (.out(clock_1_out));
  Multiplexer #(.enable("false")) multiplexer_2 (.in0(clock_1_out), .in1(1'b0), .out(clock), .sel(halt));
  ID___EX id_ex_1 (
    .WB(control_unit_1_memtoreg), .M(control_unit_1_branch), .EX(control_unit_1_aluop1), .PC_1(out_5),
    .r1(registerfile_1_data1), .r2(registerfile_1_data2), .w(multiplexer_1_out), .imm(bit_extender_1_out),
    .WB_2({exwrite, id_ex_1_wb_2[0]}), .M_2(id_ex_1_m_2), .EX_2(id_ex_1_ex_2), .PC_1_2(out_2),
    .r1_2(id_ex_1_r1_2), .r2_2(id_ex_1_r2_2), .w_2(out_9), .imm_2(id_ex_1_imm_2), .clock(clock),
    .reset(hazard_flushid), .halt(control_unit_1_halt), .halt_2(id_ex_1_halt_2));
  Subtractor #(.width(16)) subtractor_1 (.a(out_2), .b(16'h1), .out(subtractor_1_out));  // open: bin, bout
  Multiplexer #(.width(16)) multiplexer_3 (
    .in0(id_ex_1_r2_2), .in1(id_ex_1_imm_2), .out(multiplexer_3_out), .sel(id_ex_1_ex_2[4]));  // open: en
  Register #(.width(16)) register_2 (.D(out_4), .en(rread), .Q(register_2_q), .clk(clock));  // open: clr
  Adder #(.width(16)) adder_2 (.a(subtractor_1_out), .b(id_ex_1_imm_2), .out(adder_2_out));  // open: cin, cout
  ALU alu_1 (
    .Data1(id_ex_1_r1_2), .Data2(multiplexer_3_out), .ALU_sel(alu_control_1_alu_control_output),
    .ALU_result(alu_1_alu_result), .BLE_ZERO(alu_1_ble_zero));  // open: _0000data1self, _0001plus, _0010and, _0011or, _0100negdata1, SLT0110, shiftleft0111, shiftright1000, _1001, out_15
  ALU_Control alu_control_1 (
    .ALUop1(id_ex_1_ex_2[0]), .ALUop2(id_ex_1_ex_2[1]), .ALUop3(id_ex_1_ex_2[2]), .ALUop4(id_ex_1_ex_2[3]),
    .ALU_control_output(alu_control_1_alu_control_output));  // open: out_5
  ALU_Control2 alu_control2_1 (
    .ALUop1(id_ex_1_ex_2[0]), .ALUop2(id_ex_1_ex_2[1]), .ALUop3(id_ex_1_ex_2[2]), .ALUop4(id_ex_1_ex_2[3]),
    .jump(alu_control2_1_jump), .call(alu_control2_1_call), .rtn(alu_control2_1_rtn),
    .reboot(alu_control2_1_reboot));
  Multiplexer #(.width(16)) multiplexer_4 (
    .in0(out_2), .in1(adder_2_out), .out(multiplexer_4_out), .sel(and_1_out));  // open: en
  Adder #(.width(16)) adder_3 (.a(bit_extender_2_out), .b(subtractor_1_out), .out(adder_3_out));  // open: cin, cout
  Multiplexer #(.width(16)) multiplexer_5 (
    .in0(multiplexer_4_out), .in1(adder_3_out), .out(multiplexer_5_out), .sel(alu_control2_1_jump));  // open: en
  Multiplexer #(.width(16)) multiplexer_6 (
    .in0(multiplexer_5_out), .in1(register_2_q), .out(multiplexer_6_out), .sel(alu_control2_1_rtn));  // open: en
  and and_1 (and_1_out, id_ex_1_m_2[0], alu_1_ble_zero);
  Multiplexer #(.width(16)) multiplexer_7 (
    .in0(multiplexer_6_out), .in1({16{1'b0}}), .out(out_1), .sel(alu_control2_1_reboot));  // open: en
  or or_1 (Branch_Jump, and_1_out, alu_control2_1_jump);
  EX_MEM ex_mem_1 (
    .WB({exwrite, id_ex_1_wb_2[0]}), .M(id_ex_1_m_2[2:1]), .alu_result(alu_1_alu_result), .D(id_ex_1_r2_2),
    .w(out_9), .WB_2({memwrite, ex_mem_1_wb_2[0]}), .M_2(ex_mem_1_m_2), .ALU_result_2(ex_mem_1_alu_result_2),
    .D_2(ex_mem_1_d_2), .w_2(out_11), .clock(clock), .halt(id_ex_1_halt_2), .halt_2(ex_mem_1_halt_2),
    .raread(alu_control2_1_call), .raread_2(rread));  // open: reset
  RAM #(.addrWidth(16), .dataWidth(16), .bus("separate")) ram_1 (
    .addr(ex_mem_1_alu_result_2), .din(ex_mem_1_d_2), .data(ram_1_data), .str(ex_mem_1_m_2[1]), .clk(clock),
    .ld(ex_mem_1_m_2[0]));  // open: sel, clr
  MEM_WB mem_wb_1 (
    .WB({memwrite, ex_mem_1_wb_2[0]}), .alu_result(ex_mem_1_alu_result_2), .D(ram_1_data), .w(out_11),
    .halt(ex_mem_1_halt_2), .WB_2({w, mem_wb_1_wb_2[0]}), .alu_result_2(mem_wb_1_alu_result_2),
    .D_2(mem_wb_1_d_2), .w_2(out_7), .halt_2(halt), .clock(clock));  // open: reset
  Multiplexer #(.width(16)) multiplexer_8 (
    .in0(mem_wb_1_alu_result_2), .in1(mem_wb_1_d_2), .out(multiplexer_8_out), .sel(mem_wb_1_wb_2[0]));  // open: en

  assign out_8 = out_6[10:8];
  assign out_10 = out_6[7:5];

  // Other names for the same wires on the sheet: ex[2:0] = out_9; mem[2:0] = out_11; wreg[2:0] = out_7

  // Notes on the sheet:
  //   contents of rom_1 (hex, n*v repeats v):
  //   0 a 28 40 3200 2a60 b30 5b22 1334 9800 0 0 9800
endmodule
